# Fritzing sketch wiring (saved by Fritzing 0.9.5d)

parts:
  PowerBoost_1000C = Adafruit PowerBoost 1000C [part_number="Adafruit #2465"]
  Proximity_Sensor = Adafruit VCNL4010 Proximity and Light sensor [part_number="Adafruit #466"]
  DS18B20_1-Wire_Temperature_Sensor_Probe = DS18B20 1-Wire Temperature Sensor Probe Cable
  Motor_Controller = Adafruit DRV8833 DC/Stepper Motor Driver [part_number="Adafruit #3297"]
  M1 = DC Motor
  DC_Motors = DC Motor
  Arduino_nano_33_IoT = Arduino Nano 33 IOT-tht
  Pixy2_camera_systems = TTL Serial JPEG Camera
  R1 = Resistor [tolerance=±5% resistance=3.3k package=THT]
  R2 = Resistor [tolerance=±5% resistance=10k package=THT]
  Qi_Receiver = Camdenboss CTB0158-2 [part_number=CTB0158-2 package=THT]
  R3 = Resistor [tolerance=±5% resistance=330 package=THT]
  APA_LED_106 = ws2812b [package="smd 2812b"]
  LiPo_3000mAh = LIPO-3000mAh [package=lipo-3000]
  Part1 = Adafruit PowerRelay Feather Wing [part_number="Adafruit #3191"]
  Transistor_2A2222A = NPN-Transistor [package="SOT-23 [SMD]"]
  R4 = Resistor [tolerance=±5% resistance=1k package="2010 [SMD]"]
  R5 = Resistor [tolerance=±5% resistance=12k package="2010 [SMD]"]
  R6 = Resistor [tolerance=±5% resistance=10k package="2010 [SMD]"]

nets:
  GND: PowerBoost_1000C.GND, Proximity_Sensor.GND, DS18B20_1-Wire_Temperature_Sensor_Probe.GND, Motor_Controller.GND, Arduino_nano_33_IoT.pin_14, Arduino_nano_33_IoT.pin_19, Pixy2_camera_systems.GND, R2.Pin_1, APA_LED_106.VSS, LiPo_3000mAh.-, Part1.GND, R6.Pin_0
  N1: PowerBoost_1000C.VBUS, Part1.NO
  N2: PowerBoost_1000C.VLIPO, Transistor_2A2222A.1
  N3: PowerBoost_1000C.VBAT, Motor_Controller.VMOTOR, R1.Pin_0, LiPo_3000mAh.+
  N4: PowerBoost_1000C.ENABLE, Transistor_2A2222A.2
  VDD: PowerBoost_1000C.5.0V, Proximity_Sensor.VIN, DS18B20_1-Wire_Temperature_Sensor_Probe.VDD, Arduino_nano_33_IoT.pin_15, Pixy2_camera_systems.5V, APA_LED_106.VDD
  N5: Proximity_Sensor.SDA, Arduino_nano_33_IoT.pin_8
  N6: Proximity_Sensor.SCL, Arduino_nano_33_IoT.pin_9
  N7: DS18B20_1-Wire_Temperature_Sensor_Probe.DQ, Arduino_nano_33_IoT.pin_20
  N8: Motor_Controller.AOUT2, M1.pin_1
  N9: Motor_Controller.AOUT1, M1.pin_2
  N10: Motor_Controller.BOUT1, DC_Motors.pin_1
  N11: Motor_Controller.BOUT2, DC_Motors.pin_2
  N12: Motor_Controller.BIN1, Arduino_nano_33_IoT.pin_23
  N13: Motor_Controller.BIN2, Arduino_nano_33_IoT.pin_24
  N14: Motor_Controller.AIN2, Arduino_nano_33_IoT.pin_22
  N15: Motor_Controller.AIN1, Arduino_nano_33_IoT.pin_21
  N16: Arduino_nano_33_IoT.pin_1, R5.Pin_0
  N17: Arduino_nano_33_IoT.pin_2, Part1.3.3V
  N18: Arduino_nano_33_IoT.pin_4, R1.Pin_1, R2.Pin_0
  N19: Arduino_nano_33_IoT.pin_16, Pixy2_camera_systems.TX
  N20: Arduino_nano_33_IoT.pin_17, Pixy2_camera_systems.RX
  N21: Arduino_nano_33_IoT.pin_25, R4.Pin_1
  N22: Arduino_nano_33_IoT.pin_26, R3.Pin_0
  N23: Arduino_nano_33_IoT.pin_27, Part1.RELAY
  N24: Qi_Receiver.pin2, Part1.COM
  N25: Qi_Receiver.terminal_2, R5.Pin_1
  N26: R3.Pin_1, APA_LED_106.DIN

custom parts:
  Adafruit PowerBoost 1000C: PowerBoost 1000C is the perfect power supply for your portable project! With a built-in load-sharing battery charger circuit, you'll be able to keep your power-hungry project running even while recharging the battery! This little DC/DC boost converter module can be powered by any 3.7V LiIon/LiPoly battery, and convert the battery output to 5.2V DC for running your 5V projects.
  Adafruit VCNL4010 Proximity and Light sensor: The VCNL4010 sensor is a nice way to add a small-distance proximity sensor to your microcontroller project. For longer distances (in the range of cm, you can use a SHARP IR distance sensor, but those are only good if the object is over 10 cm away. The VCNL4010 is designed for much shorter distances, no more than 200mm (about 7.5") and under our experimentation we found it worked best at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
  Adafruit DRV8833 DC/Stepper Motor Driver: Spin two DC motors or step one bi-polar or uni-polar stepper with up to 1.2A per channel using the DRV8833. This motor driver chip is a nice alternative to the TB6612 driver. Like that chip, you get 2 full H-bridges, but this chip is better for low voltage uses (can run from 2.7V up to 10.8V motor power) and has built in current limiting capability. We set it up for 1A current limiting so you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
  Arduino Nano 33 IOT-tht: The Arduino Nano 33 IoT is the easiest and cheapest point of entry to enhance existing devices (and creating new ones) to be part of the IoT and designing pico-network applications. Whether you are looking at building a sensor network connected to your office or home router, or if you want to create a BLE device sending data to a cellphone, the Nano 33 IoT is your one-stop-solution for many of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
  TTL Serial JPEG Camera: TTL Serial JPEG Camera with NTSC Out
  LIPO-3000mAh: 3000mAh Lipo-battery
  Adafruit PowerRelay Feather Wing: A Feather board without ambition is a Feather board without FeatherWings! This is the Power Relay FeatherWing. It gives you power to control, and control over power. Put simply, you can now turn on and off lamps, fans, solenoids, and other small appliances that run on up to 250VAC or DC power using any Feather board. Compared to our smaller Relay FeatherWings, this one can handle a beefy 1200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
